# Fritzing sketch ESP32ControlStand (saved by Fritzing 0.9.5d)
breadboards: 2

parts:
  S1 = Pushbutton [part_number=A package="[THT]"]
  S2 = Pushbutton [part_number=B package="[THT]"]
  S3 = Pushbutton [part_number=C package="[THT]"]
  S4 = Pushbutton [part_number=D package="[THT]"]
  S5 = Pushbutton [part_number=Bell package="[THT]"]
  R1 = Rotary Potentiometer (Small) [maximum_resistance=100kΩ part_number=Brake package=THT]
  R2 = Rotary Potentiometer (Small) [maximum_resistance=100kΩ part_number=Horn package=THT]
  RE1 = Rotary Encoder [part_number=Throttle package=THT]
  RE2 = Rotary Encoder [part_number=Reverser package=THT]
  Part1 = OLED Monochrome 128x32 I2C [part_number=931]
  TTGO-T1 = TTGO-T1
  LED1 = DUO LED RG [package="5 mm [THT]"]
  P1 = female pin header, 8 pins [form="♀ (female)"]
  J1 = male pin header, 8 pins [form="♂ (male)"]
  R3 = Resistor [tolerance=±5% resistance=220 package=THT]
  R4 = Resistor [tolerance=±5% resistance=220 package=THT]
  J2 = female pin header, 6 pins [form="♀ (female)"]
  J3 = male pin header, 6 pins [form="♂ (male)"]
  R5 = Resistor [tolerance=±5% resistance=100k package=THT]
  R6 = Resistor [tolerance=±5% resistance=100k package=THT]
  R7 = Resistor [tolerance=±5% resistance=100k package=THT]
  R8 = Resistor [tolerance=±5% resistance=100k package=THT]

nets:
  N1: S1.Pin_1, S1.Pin_2, P1.pin2
  N2: S1.Pin_3, S1.Pin_4, S2.Pin_3, S2.Pin_4, S3.Pin_3, S3.Pin_4, S4.Pin_3, S4.Pin_4, S5.Pin_3, S5.Pin_4, LED1.common_cathode, P1.pin1
  N3: S2.Pin_1, S2.Pin_2, P1.pin3
  N4: S3.Pin_1, S3.Pin_2, P1.pin4
  N5: S4.Pin_1, S4.Pin_2, P1.pin5
  N6: S5.Pin_1, S5.Pin_2, P1.pin6
  GND: R1.leg1, R2.leg1, RE1.EncoderPinC, TTGO-T1.GND, J1.pin1, J3.pin3, R8.Pin_1
  Brake: R1.wiper, TTGO-T1.SVN
  3.3V: R1.leg2, R2.leg2, TTGO-T1.3v3, TTGO-T1.SD3, R6.Pin_0, R7.Pin_0
  Horn: R2.wiper, TTGO-T1.SVP
  ThrottleA: RE1.EncoderPinA, TTGO-T1.D23
  ThrottleB: RE1.EncoderPinB, TTGO-T1.D19
  N7: RE2.EncoderPinA, R6.Pin_1
  Reverser: RE2.EncoderPinC, TTGO-T1.D27, R8.Pin_0
  N8: RE2.EncoderPinB, R5.Pin_1
  N9: Part1.VIN, J2.pin1
  N10: Part1.3.3V, J2.pin2
  N11: Part1.GND, J2.pin3
  N12: Part1.RESET, J2.pin4
  N13: Part1.SCL, J2.pin5
  N14: Part1.SDA, J2.pin6
  RST: TTGO-T1.RST, J3.pin4
  Button_A: TTGO-T1.D34, J1.pin2
  Button_B: TTGO-T1.D35, J1.pin3
  Status_G: TTGO-T1.D32, R4.Pin_1
  Button_C: TTGO-T1.D33, J1.pin4
  Button_D: TTGO-T1.D25, J1.pin5
  Bell: TTGO-T1.D26, J1.pin6
  SCLK: TTGO-T1.D14
  Status_R: TTGO-T1.D12, R3.Pin_1
  SDA: TTGO-T1.D13, TTGO-T1.D21, J3.pin6
  L_Ditch: TTGO-T1.D0
  CAN_RX: TTGO-T1.D4
  L_Bright: TTGO-T1.D16
  L_Dim: TTGO-T1.D17
  CAN_TX: TTGO-T1.D5
  L_Off: TTGO-T1.D18
  5V: TTGO-T1.5V, J3.pin1
  SCL: TTGO-T1.D22, J3.pin5
  N15: LED1.red_anode, P1.pin8
  N16: LED1.green_anode, P1.pin7
  N17: J1.pin7, R4.Pin_0
  N18: J1.pin8, R3.Pin_0
  N19: R5.Pin_0, R7.Pin_1

custom parts:
  OLED Monochrome 128x32 I2C: These displays are small, only about 1" diagonal, but very readable due to the high contrast of an OLED display. This display is made of 128x32 individual white OLED pixels, each one is turned on or off by the controller chip. Because the display makes its own light, no backlight is required. This reduces the power required to run the OLED and is why the display has such high contrast; we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
  TTGO-T1: The TTGO-1 is a complete USB-based microcontoller development system, based on the ESP32 processor, in a very small footprint, capable of implementing many types of projects. All programming is done via the USB port. No special programmer is needed, only a standard micro-USB cable and a PC or Macintosh with a USB port.
  DUO LED RG: A 5mm DUO-color LED with red and green inside. Pin order: red - com. cathode - green
